// Logisim project Logisim-129-140.circ as structural Verilog: 6 circuits, main circuit main
module main (
  input  Player_1,
  input  Player_2,
  input  Player_3,
  input  Player_4
);

  wire ic74147_1__6, ic74147_1__7, ic74147_1__9, ic74147_1__14, ic_7404_1__2, ic_7404_1__4, ic_7404_1__6,
       ic_7404_1__8, ic_7447_1_a, ic_7447_1_b, ic_7447_1_c, ic_7447_1_d, ic_7447_1_e, ic_7447_1_f,
       ic_7447_1_g, ic_7475_1__9, ic_7475_1__10, ic_7475_1__15, ic_7475_1__16, nand_1_out, nand_2_out,
       not_1_out, not_2_out, not_3_out, not_4_out, or_1_out;

  not not_1 (not_1_out, Player_1);
  not not_2 (not_2_out, Player_2);
  not not_3 (not_3_out, Player_3);
  not not_4 (not_4_out, Player_4);
  or or_1 (or_1_out, Player_1, Player_2, Player_3, Player_4);
  ic_7475 ic_7475_1 (
    ._2(not_1_out), ._3(not_2_out), ._6(not_3_out), ._7(not_4_out), ._13(nand_1_out), ._4(nand_1_out),
    ._16(ic_7475_1__16), ._15(ic_7475_1__15), ._10(ic_7475_1__10), ._9(ic_7475_1__9));
  nand nand_1 (nand_1_out, nand_2_out, nand_2_out, nand_2_out, or_1_out);
  nand nand_2 (nand_2_out, ic_7475_1__16, ic_7475_1__15, ic_7475_1__10, ic_7475_1__9);
  ic74147 ic74147_1 (
    ._11(ic_7475_1__16), ._12(ic_7475_1__15), ._13(ic_7475_1__10), ._1(ic_7475_1__9), ._2(1'b1), ._3(1'b1),
    ._4(1'b1), ._5(1'b1), ._10(1'b1), ._9(ic74147_1__9), ._7(ic74147_1__7), ._6(ic74147_1__6),
    ._14(ic74147_1__14));
  ic_7404 ic_7404_1 (
    ._1(ic74147_1__9), ._3(ic74147_1__7), ._5(ic74147_1__6), ._9(ic74147_1__14), ._2(ic_7404_1__2),
    ._4(ic_7404_1__4), ._6(ic_7404_1__6), ._8(ic_7404_1__8));  // open: _11, _13, _10, _12
  ic_7447 ic_7447_1 (
    ._7(ic_7404_1__2), ._1(ic_7404_1__4), ._2(ic_7404_1__6), ._6(ic_7404_1__8), ._3(1'b1), ._5(1'b1),
    .a(ic_7447_1_a), .b(ic_7447_1_b), .c(ic_7447_1_c), .d(ic_7447_1_d), .e(ic_7447_1_e), .f(ic_7447_1_f),
    .g(ic_7447_1_g));
  _7_Segment_Display u_7_segment_display_1 (
    .g(ic_7447_1_g), .f(ic_7447_1_f), .a(ic_7447_1_a), .b(ic_7447_1_b), .e(ic_7447_1_e), .d(ic_7447_1_d),
    .c(ic_7447_1_c));  // open: dp

  // Notes on the sheet:
  //   Power
  //   reset
  //   How to use:
  //   Press switches of the players in any order. 
  //   To reset, switch off all the player switches.
  //   ic 7475
  //   4 bit bistable latch
  //   The player whose switch was pressed first would be displayed on the display.
  //   16CO129-16CO140
  //   FIRST     RESPONSE    DETECTOR   CIRCUIT
  //   Palak Singhal  -  16CO129 
  //   Sharanya Kamath - 16CO140
  //   ic 74147
  //   priority encoder
  //   ic 7404
  //   hex inverter
  //   ic 7447
  //   hex to 7 segment
  //   decoder
  //   7 segment display
endmodule

module d_latch (
  input  D,
  input  E,
  output Q,
  output Q_bar
);

  wire nand_1_out, nand_2_out;

  nand nand_1 (nand_1_out, D, E);
  nand nand_2 (nand_2_out, nand_1_out, E);
  nand nand_3 (Q, nand_1_out, Q_bar);
  nand nand_4 (Q_bar, Q, nand_2_out);

  // Notes on the sheet:
  //   D Latch
endmodule

module ic_7475 (
  input  _2,
  input  _3,
  input  _6,
  input  _7,
  input  _13,
  input  _4,
  output _16,
  output _15,
  output _10,
  output _9
);

  d_latch d_latch_1 (.D(_2), .E(_13), .Q(_16));  // open: Q_bar
  d_latch d_latch_2 (.D(_3), .E(_13), .Q(_15));  // open: Q_bar
  d_latch d_latch_3 (.D(_6), .E(_4), .Q(_10));  // open: Q_bar
  d_latch d_latch_4 (.D(_7), .E(_4), .Q(_9));  // open: Q_bar

  // Notes on the sheet:
  //   Input Pins
  //   IC 7475
  //   4 bit Bistable latch
  //   Output Pins
endmodule

module ic_7404 (
  input  _1,
  input  _3,
  input  _5,
  input  _9,
  input  _11,
  input  _13,
  output _2,
  output _4,
  output _6,
  output _8,
  output _10,
  output _12
);

  not not_1 (_2, _1);
  not not_2 (_4, _3);
  not not_3 (_6, _5);
  not not_4 (_8, _9);
  not not_5 (_10, _11);
  not not_6 (_12, _13);

  // Notes on the sheet:
  //   Input Pins
  //   IC 7404
  //   Hex Inverter
  //   Output Pins
endmodule

module ic74147 (
  input  _11,
  input  _12,
  input  _13,
  input  _1,
  input  _2,
  input  _3,
  input  _4,
  input  _5,
  input  _10,
  output _9,
  output _7,
  output _6,
  output _14
);

  wire and_1_out, and_2_out, and_3_out, and_4_out, and_5_out, and_6_out, and_7_out, and_8_out, and_9_out,
       and_10_out, and_11_out, and_12_out, nor_1_out, not_1_out, not_2_out, not_3_out, not_4_out, not_5_out,
       not_6_out, not_7_out, not_8_out, not_9_out, not_10_out, not_11_out, not_12_out, not_13_out;

  not not_1 (not_1_out, _11);
  not not_2 (not_2_out, _12);
  not not_3 (not_3_out, _13);
  not not_4 (not_4_out, _1);
  not not_5 (not_5_out, _2);
  not not_6 (not_6_out, _3);
  not not_7 (not_7_out, _4);
  not not_8 (not_8_out, _5);
  not not_9 (not_9_out, _10);
  not not_10 (not_10_out, not_2_out);
  not not_11 (not_11_out, not_4_out);
  not not_12 (not_12_out, not_5_out);
  not not_13 (not_13_out, not_6_out);
  nor nor_1 (nor_1_out, not_8_out, not_9_out);
  and and_1 (and_1_out, not_1_out, not_10_out, not_11_out, not_13_out, nor_1_out);
  and and_2 (and_2_out, not_3_out, not_11_out, not_13_out, nor_1_out);
  and and_3 (and_3_out, not_5_out, not_13_out, nor_1_out);
  and and_4 (and_4_out, not_7_out, nor_1_out);
  and and_5 (and_5_out, not_2_out, not_11_out, not_12_out, nor_1_out);
  and and_6 (and_6_out, not_3_out, not_11_out, not_12_out, nor_1_out);
  and and_7 (and_7_out, not_6_out, nor_1_out);
  and and_8 (and_8_out, not_7_out, nor_1_out);
  and and_9 (and_9_out, not_4_out, nor_1_out);
  and and_10 (and_10_out, not_5_out, nor_1_out);
  and and_11 (and_11_out, not_6_out, nor_1_out);
  and and_12 (and_12_out, not_7_out, nor_1_out);
  nor nor_2 (_9, and_1_out, and_2_out, and_3_out, and_4_out, not_9_out);
  nor nor_3 (_7, and_5_out, and_6_out, and_7_out, and_8_out);
  nor nor_4 (_6, and_9_out, and_10_out, and_11_out, and_12_out);
  nor nor_5 (_14, not_8_out, not_9_out);

  // Notes on the sheet:
  //   Input Pins
  //   Output Pins
  //   IC 74147
  //   Priority Encoder
endmodule

module ic_7447 (
  input  _7,
  input  _1,
  input  _2,
  input  _6,
  input  _3,
  input  _5,
  output a,
  output b,
  output c,
  output d,
  output e,
  output f,
  output g
);

  wire and_1_out, and_2_out, and_3_out, and_4_out, and_5_out, and_6_out, and_7_out, and_8_out, and_9_out,
       and_10_out, and_11_out, and_12_out, and_13_out, and_14_out, and_15_out, and_16_out, and_17_out,
       buffer_1_out, buffer_2_out, buffer_3_out, nand_1_out, nand_2_out, nand_3_out, nand_4_out, nand_5_out,
       nand_6_out, nand_7_out, nand_8_out, not_1_out, not_2_out;

  not not_1 (not_1_out, _6);
  buf buffer_1 (buffer_1_out, _3);
  nand nand_1 (nand_1_out, _7, buffer_1_out);
  nand nand_2 (nand_2_out, _1, buffer_1_out);
  nand nand_3 (nand_3_out, _2, buffer_1_out);
  not not_2 (not_2_out, _5);
  nand nand_4 (nand_4_out, nand_1_out, buffer_2_out);
  nand nand_5 (nand_5_out, nand_2_out, buffer_2_out);
  nand nand_6 (nand_6_out, nand_3_out, buffer_2_out);
  nand nand_7 (nand_7_out, not_1_out, buffer_2_out);
  nand nand_8 (nand_8_out, buffer_1_out, not_2_out, not_1_out, nand_2_out, nand_1_out);
  buf buffer_2 (buffer_2_out, nand_8_out);
  and and_1 (and_1_out, nand_5_out, nand_7_out);
  and and_2 (and_2_out, nand_1_out, nand_6_out);
  and and_3 (and_3_out, nand_4_out, nand_2_out, nand_3_out, not_1_out);
  and and_4 (and_4_out, nand_5_out, nand_7_out);
  and and_5 (and_5_out, nand_4_out, nand_2_out, nand_6_out);
  and and_6 (and_6_out, nand_1_out, nand_5_out, nand_6_out);
  and and_7 (and_7_out, nand_6_out, nand_7_out);
  and and_8 (and_8_out, nand_1_out, nand_5_out, nand_3_out);
  and and_9 (and_9_out, nand_4_out, nand_2_out, nand_3_out);
  and and_10 (and_10_out, nand_1_out, nand_2_out, nand_6_out);
  and and_11 (and_11_out, nand_4_out, nand_5_out, nand_6_out);
  buf buffer_3 (buffer_3_out, nand_4_out);
  and and_12 (and_12_out, nand_2_out, nand_6_out);
  and and_13 (and_13_out, nand_4_out, nand_5_out);
  and and_14 (and_14_out, nand_5_out, nand_3_out);
  and and_15 (and_15_out, nand_4_out, not_1_out, nand_3_out);
  and and_16 (and_16_out, nand_4_out, nand_5_out, nand_6_out);
  and and_17 (and_17_out, nand_2_out, nand_3_out, not_1_out, buffer_1_out);
  nor nor_1 (c, and_7_out, and_8_out);
  nor nor_2 (d, and_9_out, and_10_out, and_11_out);
  nor nor_3 (e, buffer_3_out, and_12_out);
  nor nor_4 (a, and_1_out, and_2_out, and_3_out);
  nor nor_5 (b, and_4_out, and_5_out, and_6_out);
  nor nor_6 (f, and_13_out, and_14_out, and_15_out);
  nor nor_7 (g, and_16_out, and_17_out);

  // Notes on the sheet:
  //   Input Pins
  //   IC 7447
  //   Hex to 7 Segment Decoder
  //   Output Pins
endmodule
